# Fritzing sketch sketch (saved by Fritzing 0.9.3b)
breadboards: 1

parts:
  Raspberry_Pi_1 = Raspberry Pi 3 [part_number=RPI-3-V1.2]
  LED1 = LED - 5mm [color="Red (633nm)" package="5 mm [THT]"]
  R1 = Resistor [tolerance=±5% resistance=10k package=THT]
  R2 = Resistor [tolerance=±5% resistance=10k package=THT]
  LED2 = LED - 5mm [color="Red (633nm)" package="5 mm [THT]"]
  R3 = Resistor [tolerance=±5% resistance=10k package=THT]
  LED3 = LED - 5mm [color="Red (633nm)" package="5 mm [THT]"]
  R4 = Resistor [tolerance=±5% resistance=10k package=THT]
  LED4 = LED - 5mm [color="Red (633nm)" package="5 mm [THT]"]
  R5 = Resistor [tolerance=±5% resistance=10k package=THT]
  LED5 = LED - 5mm [color="Red (633nm)" package="5 mm [THT]"]
  R6 = Resistor [tolerance=±5% resistance=10k package=THT]
  LED6 = LED - 5mm [color="Red (633nm)" package="5 mm [THT]"]

nets:
  N1: Raspberry_Pi_1.GPIO25, R6.Pin_0
  N2: Raspberry_Pi_1.GND, LED1.cathode, LED2.cathode, LED3.cathode, LED4.cathode, LED5.cathode, LED6.cathode
  N3: Raspberry_Pi_1.GPIO24, R5.Pin_0
  N4: Raspberry_Pi_1.GPIO18, R3.Pin_0
  N5: Raspberry_Pi_1.GPIO15, R2.Pin_0
  N6: Raspberry_Pi_1.GPIO14, R1.Pin_0
  N7: LED1.anode, R1.Pin_1
  N8: R2.Pin_1, LED2.anode
  N9: R3.Pin_1, LED3.anode
  N10: R4.Pin_1, LED4.anode
  N11: R5.Pin_1, LED5.anode
  N12: R6.Pin_1, LED6.anode
