# Fritzing sketch dht11 (saved by Fritzing 0.9.3b)
breadboards: 1

parts:
  Part1 = Arduino Uno (Rev3)
  U1 = mystery part, 4 pins [chip_label=DHT11]
  R1 = Resistor [tolerance=±5% resistance=10k package=THT]

nets:
  N1: Part1.D2, U1.pin2, R1.Pin_0
  N2: Part1.5V, U1.pin1, R1.Pin_1
  N3: Part1.GND, U1.pin4
